# Fritzing sketch main_bb (saved by Fritzing 0.9.3b)

parts:
  Part1 = RFID-RC522-v3
  Part2 = Arduino Uno (Rev3)
  Part3 = KY-012 Active Buzzer Module [package="Breakout board"]
  J1 = Basic Servo

nets:
  N1: Part1.SDA, Part2.D10_PWM/SS
  N2: Part1.SCK, Part2.D13/SCK
  N3: Part1.MOSI, Part2.D11_PWM/MOSI
  N4: Part1.MISO, Part2.D12/MISO
  GND: Part1.GND, Part2.GND, Part3.-, J1.gnd
  N5: Part1.RST, Part2.D9_PWM
  3.3V: Part1.3.3V, Part2.3V3
  N6: Part2.D6_PWM, J1.pulse
  5V: Part2.5V, Part3.S, J1.vcc

custom parts:
  RFID-RC522-v3: A simple China made RFID-RC522 Reader (6x4 cm); do check the pin labels, as this is a MFRC522 based clone.
  KY-012 Active Buzzer Module: Active Piezoelectric Buzzer Module Keyes KY-012, it produces single-tone sound when signal is high.
